# Fritzing sketch ESP32-S3-WROOM-N16R8_Devkit (saved by Fritzing 1.0.2b)
circuit board: 19.0243cm x 10.8863cm
breadboards: 2

parts:
  Header_GND_tm_3V3 = female pin header, 22 pins [form="♀ (female)"]
  HEADER_GND_tm_GND = female pin header, 22 pins [form="♀ (female)"]
  US_Top = AJ-SR04M Module [part_number=AJ-SR04M]
  US_Bottom = AJ-SR04M Module [part_number=AJ-SR04M]
  Mic = INMP441
  A1 = ESP32-S3-WROOM-1-N16R8 dev board  # not connected

nets:
  N1: Header_GND_tm_3V3.pin1, Mic.VDD
  N2: Header_GND_tm_3V3.pin4, Mic.SD
  N3: Header_GND_tm_3V3.pin5, Mic.SCK
  N4: Header_GND_tm_3V3.pin6, Mic.WS
  VCC: Header_GND_tm_3V3.pin21, US_Top.VCC, US_Bottom.VCC
  GND: HEADER_GND_tm_GND.pin1, HEADER_GND_tm_GND.pin2, US_Top.GND, US_Bottom.GND, Mic.L/R, Mic.GND
  N5: HEADER_GND_tm_GND.pin4, US_Top.Echo
  N6: HEADER_GND_tm_GND.pin5, US_Top.Trig
  N7: HEADER_GND_tm_GND.pin19, US_Bottom.Echo
  N8: HEADER_GND_tm_GND.pin20, US_Bottom.Trig

custom parts:
  AJ-SR04M Module: AJ-SR04M Ultrasonic Distance Measuring Sensor Controller Module, 3-5V DC.
  INMP441: This is a simple breakout board for the INMP441 I2S MEMS microphone.
  ESP32-S3-WROOM-1-N16R8 dev board: ESP32-S3 WIFI+BLE5.0 Development Board ESP32-S3-WROOM-1-N16R8(16M Flash/8SRAM).
